// Logisim project CRC.circ as structural Verilog
module CRC (
  input  [7:0] A,
  input  [3:0] B,
  output [10:0] C
);

  wire four_1__0_2, four_1__1_2, four_1__2_2, four_2__0_2, four_2__1_2, four_2__2_2, four_3__0_2,
       four_3__1_2, four_3__2_2, four_4__0_2, four_4__1_2, four_4__2_2, four_5__0_2, four_5__1_2,
       four_5__2_2, four_6__0_2, four_6__1_2, four_6__2_2, four_7__0_2, four_7__1_2, four_7__2_2, S3, S4, S5,
       S6, S7, S8, S9, S10;

  four four_1 (
    ._0(A[4]), ._1(A[5]), ._2(A[6]), ._3(A[7]), .B(B), .S(S10), ._0_2(four_1__0_2), ._1_2(four_1__1_2),
    ._2_2(four_1__2_2));
  four four_2 (
    ._0(A[3]), ._1(four_1__0_2), ._2(four_1__1_2), ._3(four_1__2_2), .B(B), .S(S9), ._0_2(four_2__0_2),
    ._1_2(four_2__1_2), ._2_2(four_2__2_2));
  four four_3 (
    ._0(A[2]), ._1(four_2__0_2), ._2(four_2__1_2), ._3(four_2__2_2), .B(B), .S(S8), ._0_2(four_3__0_2),
    ._1_2(four_3__1_2), ._2_2(four_3__2_2));
  four four_4 (
    ._0(A[1]), ._1(four_3__0_2), ._2(four_3__1_2), ._3(four_3__2_2), .B(B), .S(S7), ._0_2(four_4__0_2),
    ._1_2(four_4__1_2), ._2_2(four_4__2_2));
  four four_5 (
    ._0(A[0]), ._1(four_4__0_2), ._2(four_4__1_2), ._3(four_4__2_2), .B(B), .S(S6), ._0_2(four_5__0_2),
    ._1_2(four_5__1_2), ._2_2(four_5__2_2));
  four four_6 (
    ._0(1'b0), ._1(four_5__0_2), ._2(four_5__1_2), ._3(four_5__2_2), .B(B), .S(S5), ._0_2(four_6__0_2),
    ._1_2(four_6__1_2), ._2_2(four_6__2_2));
  four four_7 (
    ._0(1'b0), ._1(four_6__0_2), ._2(four_6__1_2), ._3(four_6__2_2), .B(B), .S(S4), ._0_2(four_7__0_2),
    ._1_2(four_7__1_2), ._2_2(four_7__2_2));
  four four_8 (
    ._0(1'b0), ._1(four_7__0_2), ._2(four_7__1_2), ._3(four_7__2_2), .B(B), .S(S3), ._0_2(C[0]), ._1_2(C[1]),
    ._2_2(C[2]));

  assign C[10:3] = A;

  // Other names for the same wires on the sheet: S0 = C[0]; S1 = C[1]; S2 = C[2]; _0 = A[0]; _1 = A[1]; _2 = A[2];
  //   _3 = A[3]; _4 = A[4]; _5 = A[5]; _6 = A[6]; _7 = A[7]
endmodule

module four (
  input  _0,
  input  _1,
  input  _2,
  input  _3,
  input  [3:0] B,
  output S,
  output _0_2,
  output _1_2,
  output _2_2
);

  wire [3:0] bit_extender_1_out, multiplier_1_out;
  wire [3:3] xor_1_out;

  Comparator #(.width(1), .mode("unsigned")) comparator_1 (.a(_3), .b(1'b1), .eq(S));  // open: gt, lt
  assign bit_extender_1_out = {{3{1'b0}}, S};  // Bit_Extender bit_extender_1
  Multiplier #(.width(4)) multiplier_1 (.a(bit_extender_1_out), .b(B), .out(multiplier_1_out));  // open: cin, cout
  assign {xor_1_out[3], _2_2, _1_2, _0_2} = multiplier_1_out ^ {_3, _2, _1, _0};  // XOR_Gate xor_1, 4 bits wide

  // Notes on the sheet:
  //   3210
endmodule
