// Logisim project Mealy.circ as structural Verilog
module fsm (
  input  CLR,
  input  [1:0] In,
  output Z
);

  wire _0, _1, clk, counter_2_q, not_1_out, reset, S0, S00, S1, S11;

  Clock clock_1 (.out(clk));
  not not_1 (not_1_out, CLR);
  // Probe on In[1]
  Counter #(.width(1), .max('h1)) counter_1 (.Q(reset), .clk(clk), .clr(not_1_out));  // open: load, D, count, carry
  // Probe on In[0]
  Counter #(.width(1), .max('h1), .ongoal("stay")) counter_2 (
    .Q(counter_2_q), .clk(clk), .clr(reset));  // open: load, D, count, carry
  \状态转移  \u_状态转移_1  (.S1(_1), .S0(_0), .TA(In[1]), .TB(In[0]), .S11(S11), .S00(S00));
  Multiplexer multiplexer_1 (.in0(1'b0), .in1(S0), .out(_0), .sel(counter_2_q));  // open: en
  Multiplexer multiplexer_2 (.in0(1'b0), .in1(S1), .out(_1), .sel(counter_2_q));  // open: en
  // Probe on S1
  Register #(.width(1)) register_1 (.D(S11), .Q(S1), .clk(clk), .clr(reset));  // open: en
  // Probe on S0
  Register #(.width(1)) register_2 (.D(S00), .Q(S0), .clk(clk), .clr(reset));  // open: en
  \输出  \u_输出_1  (.S1(S1), .S0(S0), .TA(In[1]), .TB(In[0]), .Z(Z));

  // Other names for the same wires on the sheet: TB = In[0]; TA = In[1]

  // Notes on the sheet:
  //   需要一种异步复位的实现方式
  //   其实用多路选择器即可实现同步复位
endmodule

module \状态转移  (
  input  S1,
  input  S0,
  input  TA,
  input  TB,
  output S11,
  output S00
);

  wire and_1_out, and_2_out, and_3_out, and_4_out, and_5_out, and_6_out, and_7_out, and_8_out, not_1_out,
       not_2_out, not_3_out, not_4_out, not_5_out, not_6_out, not_7_out, not_8_out, not_9_out, not_10_out,
       not_11_out, not_12_out, not_13_out, not_14_out, not_15_out, not_16_out;

  not not_1 (not_1_out, S1);
  and and_1 (and_1_out, not_1_out, S0, not_2_out);
  not not_2 (not_2_out, TA);
  not not_3 (not_3_out, S1);
  and and_2 (and_2_out, not_3_out, S0, not_4_out);
  not not_4 (not_4_out, TB);
  and and_3 (and_3_out, S1, not_5_out, not_6_out);
  not not_5 (not_5_out, S0);
  not not_6 (not_6_out, TA);
  not not_7 (not_7_out, S0);
  and and_4 (and_4_out, S1, not_7_out, not_8_out);
  not not_8 (not_8_out, TB);
  not not_9 (not_9_out, S1);
  not not_10 (not_10_out, S0);
  not not_11 (not_11_out, TA);
  not not_12 (not_12_out, S1);
  not not_13 (not_13_out, TB);
  not not_14 (not_14_out, S0);
  not not_15 (not_15_out, TB);
  not not_16 (not_16_out, TA);
  or or_1 (S11, and_1_out, and_2_out, and_3_out, and_4_out);
  and and_5 (and_5_out, not_9_out, not_10_out, not_11_out, TB);
  and and_6 (and_6_out, not_12_out, S0, not_13_out);
  and and_7 (and_7_out, S1, not_14_out, not_15_out);
  and and_8 (and_8_out, S1, S0, not_16_out, TB);
  or or_2 (S00, and_5_out, and_6_out, and_7_out, and_8_out);
endmodule

module \输出  (
  input  S1,
  input  S0,
  input  TA,
  input  TB,
  output Z
);

  wire not_1_out;

  and and_1 (Z, S1, S0, not_1_out);
  not not_1 (not_1_out, TB);
endmodule
