// Logisim project grf.circ as structural Verilog: 2 circuits, main circuit main
module main (
);

  grf grf_1 ();  // open: clk, reset, WD, WE, A3, A1, A2, RD1, RD2
endmodule

module grf (
  input  clk,
  input  reset,
  input  [31:0] WD,
  input  WE,
  input  [4:0] A3,
  input  [4:0] A1,
  input  [4:0] A2,
  output [31:0] RD1,
  output [31:0] RD2
);

  wire [31:0] _0, _1, _2, _3, _4, _5, _6, _7, _8, _9, _10, _11, _12, _13, _14, _15, _16, _17, _18, _19, _20,
       _21, _22, _23, _24, _25, _26, _27, _28, _29, _30, _31, demultiplexer_1_out1, demultiplexer_1_out2,
       demultiplexer_1_out3, demultiplexer_1_out4, demultiplexer_1_out5, demultiplexer_1_out6,
       demultiplexer_1_out7, demultiplexer_1_out8, demultiplexer_1_out9, demultiplexer_1_out10,
       demultiplexer_1_out11, demultiplexer_1_out12, demultiplexer_1_out13, demultiplexer_1_out14,
       demultiplexer_1_out15, demultiplexer_1_out16, demultiplexer_1_out17, demultiplexer_1_out18,
       demultiplexer_1_out19, demultiplexer_1_out20, demultiplexer_1_out21, demultiplexer_1_out22,
       demultiplexer_1_out23, demultiplexer_1_out24, demultiplexer_1_out25, demultiplexer_1_out26,
       demultiplexer_1_out27, demultiplexer_1_out28, demultiplexer_1_out29, demultiplexer_1_out30,
       demultiplexer_1_out31;

  Demultiplexer #(.select(5), .width(32), .tristate("true")) demultiplexer_1 (
    .out1(demultiplexer_1_out1), .out2(demultiplexer_1_out2), .out3(demultiplexer_1_out3),
    .out4(demultiplexer_1_out4), .out5(demultiplexer_1_out5), .out6(demultiplexer_1_out6),
    .out7(demultiplexer_1_out7), .out8(demultiplexer_1_out8), .out9(demultiplexer_1_out9),
    .out10(demultiplexer_1_out10), .out11(demultiplexer_1_out11), .out12(demultiplexer_1_out12),
    .out13(demultiplexer_1_out13), .out14(demultiplexer_1_out14), .out15(demultiplexer_1_out15),
    .out16(demultiplexer_1_out16), .out17(demultiplexer_1_out17), .out18(demultiplexer_1_out18),
    .out19(demultiplexer_1_out19), .out20(demultiplexer_1_out20), .out21(demultiplexer_1_out21),
    .out22(demultiplexer_1_out22), .out23(demultiplexer_1_out23), .out24(demultiplexer_1_out24),
    .out25(demultiplexer_1_out25), .out26(demultiplexer_1_out26), .out27(demultiplexer_1_out27),
    .out28(demultiplexer_1_out28), .out29(demultiplexer_1_out29), .out30(demultiplexer_1_out30),
    .out31(demultiplexer_1_out31), .in(WD), .sel(A3), .en(WE));  // open: out0
  Register #(.width(32)) u__0 (.D({32{1'b0}}), .Q(_0), .clk(clk), .clr(reset));  // open: en
  Register #(.width(32)) u__1 (.D(demultiplexer_1_out1), .Q(_1), .clk(clk), .clr(reset));  // open: en
  Register #(.width(32)) _1_2 (.D(demultiplexer_1_out2), .Q(_2), .clk(clk), .clr(reset));  // open: en
  Register #(.width(32)) _1_3 (.D(demultiplexer_1_out3), .Q(_3), .clk(clk), .clr(reset));  // open: en
  Register #(.width(32)) _1_4 (.D(demultiplexer_1_out4), .Q(_4), .clk(clk), .clr(reset));  // open: en
  Register #(.width(32)) _1_5 (.D(demultiplexer_1_out5), .Q(_5), .clk(clk), .clr(reset));  // open: en
  Register #(.width(32)) _1_6 (.D(demultiplexer_1_out6), .Q(_6), .clk(clk), .clr(reset));  // open: en
  Register #(.width(32)) _1_7 (.D(demultiplexer_1_out7), .Q(_7), .clk(clk), .clr(reset));  // open: en
  Register #(.width(32)) _1_8 (.D(demultiplexer_1_out9), .Q(_9), .clk(clk), .clr(reset));  // open: en
  Register #(.width(32)) _1_9 (.D(demultiplexer_1_out10), .Q(_10), .clk(clk), .clr(reset));  // open: en
  Register #(.width(32)) _1_10 (.D(demultiplexer_1_out11), .Q(_11), .clk(clk), .clr(reset));  // open: en
  Register #(.width(32)) _1_11 (.D(demultiplexer_1_out12), .Q(_12), .clk(clk), .clr(reset));  // open: en
  Register #(.width(32)) _1_12 (.D(demultiplexer_1_out13), .Q(_13), .clk(clk), .clr(reset));  // open: en
  Register #(.width(32)) _1_13 (.D(demultiplexer_1_out14), .Q(_14), .clk(clk), .clr(reset));  // open: en
  Register #(.width(32)) _1_14 (.D(demultiplexer_1_out15), .Q(_15), .clk(clk), .clr(reset));  // open: en
  Register #(.width(32)) _1_15 (.D(demultiplexer_1_out16), .Q(_16), .clk(clk), .clr(reset));  // open: en
  Register #(.width(32)) _1_16 (.D(demultiplexer_1_out17), .Q(_17), .clk(clk), .clr(reset));  // open: en
  Register #(.width(32)) _1_17 (.D(demultiplexer_1_out18), .Q(_18), .clk(clk), .clr(reset));  // open: en
  Register #(.width(32)) _1_18 (.D(demultiplexer_1_out19), .Q(_19), .clk(clk), .clr(reset));  // open: en
  Register #(.width(32)) _1_19 (.D(demultiplexer_1_out20), .Q(_20), .clk(clk), .clr(reset));  // open: en
  Register #(.width(32)) _1_20 (.D(demultiplexer_1_out21), .Q(_21), .clk(clk), .clr(reset));  // open: en
  Register #(.width(32)) _1_21 (.D(demultiplexer_1_out22), .Q(_22), .clk(clk), .clr(reset));  // open: en
  Register #(.width(32)) _1_22 (.D(demultiplexer_1_out23), .Q(_23), .clk(clk), .clr(reset));  // open: en
  Register #(.width(32)) _1_23 (.D(demultiplexer_1_out24), .Q(_24), .clk(clk), .clr(reset));  // open: en
  Register #(.width(32)) _1_24 (.D(demultiplexer_1_out25), .Q(_25), .clk(clk), .clr(reset));  // open: en
  Register #(.width(32)) _1_25 (.D(demultiplexer_1_out26), .Q(_26), .clk(clk), .clr(reset));  // open: en
  Register #(.width(32)) _1_26 (.D(demultiplexer_1_out27), .Q(_27), .clk(clk), .clr(reset));  // open: en
  Register #(.width(32)) _1_27 (.D(demultiplexer_1_out28), .Q(_28), .clk(clk), .clr(reset));  // open: en
  Register #(.width(32)) _1_28 (.D(demultiplexer_1_out29), .Q(_29), .clk(clk), .clr(reset));  // open: en
  Register #(.width(32)) _1_29 (.D(demultiplexer_1_out30), .Q(_30), .clk(clk), .clr(reset));  // open: en
  Register #(.width(32)) _1_30 (.D(demultiplexer_1_out31), .Q(_31), .clk(clk), .clr(reset));  // open: en
  Register #(.width(32)) _1_31 (.D(demultiplexer_1_out8), .Q(_8), .clk(clk), .clr(reset));  // open: en
  Multiplexer #(.select(5), .width(32)) multiplexer_1 (
    .in0(_0), .in1(_1), .in2(_2), .in3(_3), .in4(_4), .in5(_5), .in6(_6), .in7(_7), .in8(_8), .in9(_9),
    .in10(_10), .in11(_11), .in12(_12), .in13(_13), .in14(_14), .in15(_15), .in16(_16), .in17(_17),
    .in18(_18), .in19(_19), .in20(_20), .in21(_21), .in22(_22), .in23(_23), .in24(_24), .in25(_25),
    .in26(_26), .in27(_27), .in28(_28), .in29(_29), .in30(_30), .in31(_31), .out(RD1), .sel(A1));  // open: en
  Multiplexer #(.select(5), .width(32)) multiplexer_2 (
    .in0(_0), .in1(_1), .in2(_2), .in3(_3), .in4(_4), .in5(_5), .in6(_6), .in7(_7), .in8(_8), .in9(_9),
    .in10(_10), .in11(_11), .in12(_12), .in13(_13), .in14(_14), .in15(_15), .in16(_16), .in17(_17),
    .in18(_18), .in19(_19), .in20(_20), .in21(_21), .in22(_22), .in23(_23), .in24(_24), .in25(_25),
    .in26(_26), .in27(_27), .in28(_28), .in29(_29), .in30(_30), .in31(_31), .out(RD2), .sel(A2));  // open: en
endmodule
