// Logisim project navigation.circ as structural Verilog
module navigation (
  input  [1:0] dir,
  input  clk,
  input  reset,
  output arrive,
  output hit
);

  wire comparator_1_eq, comparator_2_eq, invalid;
  wire [2:0] multiplexer_1_out, multiplexer_2_out, multiplexer_3_out, multiplexer_4_out, new_x, new_y, x, y;

  new_x new_x_1 (.x(x), .move(dir), .in_3(arrive), .new_x(new_x));
  new_y new_y_1 (.y(y), .arrive(arrive), .move(dir), .new_y(new_y));
  invalid invalid_1 (.new_x(new_x), .new_y(new_y), .invalid(invalid));
  Multiplexer #(.width(3)) multiplexer_1 (.in0(new_x), .in1(x), .out(multiplexer_1_out), .sel(invalid));  // open: en
  Multiplexer #(.width(3)) multiplexer_2 (
    .in0(multiplexer_1_out), .in1(3'b000), .out(multiplexer_2_out), .sel(arrive));  // open: en
  Multiplexer #(.width(3)) multiplexer_3 (.in0(new_y), .in1(y), .out(multiplexer_3_out), .sel(invalid));  // open: en
  Multiplexer #(.width(3)) multiplexer_4 (
    .in0(multiplexer_3_out), .in1(3'b000), .out(multiplexer_4_out), .sel(arrive));  // open: en
  // Probe on x
  Register #(.width(3)) register_1 (.D(multiplexer_2_out), .Q(x), .clk(clk), .clr(reset));  // open: en
  // Probe on y
  Register #(.width(3)) register_2 (.D(multiplexer_4_out), .Q(y), .clk(clk), .clr(reset));  // open: en
  Comparator #(.width(3)) comparator_1 (.a(x), .b(3'b001), .eq(comparator_1_eq));  // open: gt, lt
  Comparator #(.width(3)) comparator_2 (.a(y), .b(3'b010), .eq(comparator_2_eq));  // open: gt, lt
  Register #(.width(1)) register_3 (.D(invalid), .Q(hit), .clk(clk), .clr(reset));  // open: en
  and and_1 (arrive, comparator_1_eq, comparator_2_eq);

  // Notes on the sheet:
  //   x的范围0-1
  //   y的范围0-2
endmodule

module new_x (
  input  [2:0] x,
  input  [1:0] move,
  input  in_3,
  output [2:0] new_x
);

  wire [2:0] adder_1_out, multiplexer_1_out;

  Multiplexer #(.select(2), .width(3)) multiplexer_1 (
    .in0(3'b000), .in1(3'b001), .in2(3'b000), .in3(3'b111), .out(multiplexer_1_out), .sel(move));  // open: en
  Adder #(.width(3)) adder_1 (.a(x), .b(multiplexer_1_out), .out(adder_1_out));  // open: cin, cout
  Multiplexer #(.width(3)) multiplexer_2 (.in0(adder_1_out), .in1(3'b000), .out(new_x), .sel(in_3));  // open: en
endmodule

module new_y (
  input  [2:0] y,
  input  arrive,
  input  [1:0] move,
  output [2:0] new_y
);

  wire [2:0] adder_1_out, multiplexer_1_out;

  Multiplexer #(.select(2), .width(3)) multiplexer_1 (
    .in0(3'b001), .in1(3'b000), .in2(3'b111), .in3(3'b000), .out(multiplexer_1_out), .sel(move));  // open: en
  Adder #(.width(3)) adder_1 (.a(y), .b(multiplexer_1_out), .out(adder_1_out));  // open: cin, cout
  Multiplexer #(.width(3)) multiplexer_2 (.in0(adder_1_out), .in1(3'b000), .out(new_y), .sel(arrive));  // open: en
endmodule

module invalid (
  input  [2:0] new_x,
  input  [2:0] new_y,
  output invalid
);

  wire and_1_out, comparator_1_eq, comparator_2_eq, comparator_3_gt, comparator_4_lt, comparator_5_gt,
       comparator_6_lt;

  Comparator #(.width(3)) comparator_1 (.a(new_x), .b(3'b001), .eq(comparator_1_eq));  // open: gt, lt
  Comparator #(.width(3)) comparator_2 (.a(new_y), .b(3'b000), .eq(comparator_2_eq));  // open: gt, lt
  and and_1 (and_1_out, comparator_1_eq, comparator_2_eq);
  Comparator #(.width(3)) comparator_3 (.a(new_x), .b(3'b001), .gt(comparator_3_gt));  // open: eq, lt
  or or_1 (invalid, and_1_out, comparator_3_gt, comparator_4_lt, comparator_5_gt, comparator_6_lt);
  Comparator #(.width(3)) comparator_4 (.a(new_x), .b(3'b000), .lt(comparator_4_lt));  // open: gt, eq
  Comparator #(.width(3)) comparator_5 (.a(new_y), .b(3'b010), .gt(comparator_5_gt));  // open: eq, lt
  Comparator #(.width(3)) comparator_6 (.a(new_y), .b(3'b000), .lt(comparator_6_lt));  // open: gt, eq
endmodule
