// Logisim project 推箱子.circ as structural Verilog: 4 circuits, main circuit main
module main (
);

  Sokoban sokoban_1 ();  // open: dx, dy, clk, reset, out, flag
endmodule

module Sokoban (
  input  dx,
  input  dy,
  input  clk,
  input  reset,
  output out,
  output flag
);

  wire comparator_1_eq, comparator_2_eq, invalid;
  wire [2:0] multiplexer_1_out, multiplexer_2_out, new_x, new_y, x, y;

  // Probe on x
  // Probe on y
  invalid invalid_1 (.new_x(new_x), .new_y(new_y), .invalid(invalid));
  newx_cnt newx_cnt_1 (.x(x), .dx(dx), .out_3(new_x));
  // Probe on new_y
  newx_cnt newx_cnt_2 (.x(y), .dx(dy), .out_3(new_y));
  Multiplexer #(.width(3)) multiplexer_1 (.in0(new_x), .in1(x), .out(multiplexer_1_out), .sel(invalid));  // open: en
  Register #(.width(3)) register_1 (.D(multiplexer_1_out), .Q(x), .clk(clk), .clr(reset));  // open: en
  Register #(.width(3)) register_2 (.D(multiplexer_2_out), .Q(y), .clk(clk), .clr(reset));  // open: en
  Multiplexer #(.width(3)) multiplexer_2 (.in0(new_y), .in1(y), .out(multiplexer_2_out), .sel(invalid));  // open: en
  Register #(.width(1)) register_3 (.D(invalid), .Q(flag), .clk(clk), .clr(reset));  // open: en
  Comparator #(.width(3)) comparator_1 (.a(x), .b(3'b101), .eq(comparator_1_eq));  // open: gt, lt
  Comparator #(.width(3)) comparator_2 (.a(y), .b(3'b101), .eq(comparator_2_eq));  // open: gt, lt
  and and_1 (out, comparator_1_eq, comparator_2_eq);

  // Notes on the sheet:
  //   flag在下个周期才会置0，所以要用寄存器等一下上升沿
endmodule

module invalid (
  input  [2:0] new_x,
  input  [2:0] new_y,
  output invalid
);

  wire and_1_out, and_2_out, and_3_out, and_4_out, and_5_out, and_6_out, comparator_1_eq, comparator_2_eq,
       comparator_3_eq, comparator_4_eq, comparator_5_eq, comparator_6_eq, comparator_7_eq, comparator_8_eq,
       comparator_9_eq, comparator_10_eq, comparator_11_eq, comparator_12_eq, comparator_13_gt,
       comparator_14_lt, comparator_15_gt, comparator_16_lt, or_1_out, or_3_out;

  // Probe on new_x
  Comparator #(.width(3)) comparator_1 (.a(new_x), .b(3'b001), .eq(comparator_1_eq));  // open: gt, lt
  Comparator #(.width(3)) comparator_2 (.a(new_y), .b(3'b001), .eq(comparator_2_eq));  // open: gt, lt
  and and_1 (and_1_out, comparator_1_eq, comparator_2_eq);
  Comparator #(.width(3)) comparator_3 (.a(new_x), .b(3'b001), .eq(comparator_3_eq));  // open: gt, lt
  Comparator #(.width(3)) comparator_4 (.a(new_y), .b(3'b010), .eq(comparator_4_eq));  // open: gt, lt
  and and_2 (and_2_out, comparator_3_eq, comparator_4_eq);
  or or_1 (or_1_out, and_1_out, and_2_out, and_3_out, and_4_out, and_5_out, and_6_out);
  Comparator #(.width(3)) comparator_5 (.a(new_x), .b(3'b010), .eq(comparator_5_eq));  // open: gt, lt
  Comparator #(.width(3)) comparator_6 (.a(new_y), .b(3'b001), .eq(comparator_6_eq));  // open: gt, lt
  and and_3 (and_3_out, comparator_5_eq, comparator_6_eq);
  Comparator #(.width(3)) comparator_7 (.a(new_x), .b(3'b011), .eq(comparator_7_eq));  // open: gt, lt
  Comparator #(.width(3)) comparator_8 (.a(new_y), .b(3'b100), .eq(comparator_8_eq));  // open: gt, lt
  and and_4 (and_4_out, comparator_7_eq, comparator_8_eq);
  Comparator #(.width(3)) comparator_9 (.a(new_x), .b(3'b100), .eq(comparator_9_eq));  // open: gt, lt
  Comparator #(.width(3)) comparator_10 (.a(new_y), .b(3'b011), .eq(comparator_10_eq));  // open: gt, lt
  and and_5 (and_5_out, comparator_9_eq, comparator_10_eq);
  or or_2 (invalid, or_1_out, or_3_out);
  Comparator #(.width(3)) comparator_11 (.a(new_x), .b(3'b100), .eq(comparator_11_eq));  // open: gt, lt
  Comparator #(.width(3)) comparator_12 (.a(new_y), .b(3'b100), .eq(comparator_12_eq));  // open: gt, lt
  and and_6 (and_6_out, comparator_11_eq, comparator_12_eq);
  Comparator #(.width(3), .mode("unsigned")) comparator_13 (
    .a(new_x), .b(3'b101), .gt(comparator_13_gt));  // open: eq, lt
  Comparator #(.width(3), .mode("unsigned")) comparator_14 (
    .a(new_x), .b(3'b000), .lt(comparator_14_lt));  // open: gt, eq
  or or_3 (or_3_out, comparator_14_lt, comparator_13_gt, comparator_16_lt, comparator_15_gt);
  Comparator #(.width(3), .mode("unsigned")) comparator_15 (
    .a(new_y), .b(3'b101), .gt(comparator_15_gt));  // open: eq, lt
  Comparator #(.width(3), .mode("unsigned")) comparator_16 (
    .a(new_y), .b(3'b000), .lt(comparator_16_lt));  // open: gt, eq
endmodule

module newx_cnt (
  input  [2:0] x,
  input  dx,
  output [2:0] out_3
);

  wire [2:0] bit_extender_1_out;

  assign bit_extender_1_out = {{2{1'b0}}, dx};  // Bit_Extender bit_extender_1
  Adder #(.width(3)) adder_1 (.a(x), .b(bit_extender_1_out), .out(out_3));  // open: cin, cout
endmodule
