// Logisim project 红绿灯状态机.circ as structural Verilog: 3 circuits, main circuit main
module main (
  input  CLK,
  input  Reset,
  input  TA,
  input  TB,
  output La1,
  output La0,
  output Lb1,
  output Lb0
);

  wire not_1_out, S0, S0_prime, S1_prime;

  cnt_S1 cnt_s1_1 (.S0(S0), .S1(La1), .S1_prime(S1_prime));
  cnt_S0 cnt_s0_1 (.S1(La1), .S0(S0), .TA(TA), .TB(TB), .S0_prime(S0_prime));
  Register #(.width(1)) register_1 (.D(S1_prime), .Q(La1), .clk(CLK), .clr(Reset));  // open: en
  Register #(.width(1)) register_2 (.D(S0_prime), .Q(S0), .clk(CLK), .clr(Reset));  // open: en
  not not_1 (not_1_out, La1);
  not not_2 (Lb1, La1);
  and and_1 (La0, not_1_out, S0);
  and and_2 (Lb0, La1, S0);

  // Other names for the same wires on the sheet: S1 = La1

  // Notes on the sheet:
  //   输入
  //   次态转移逻辑
  //   次态转移逻辑可能要用到一些原态变量可以先设着
  //   S1可以用来计算S1'，S1'可以用来生成S1
  //   状态寄存器
  //   输出
endmodule

module cnt_S1 (
  input  S0,
  input  S1,
  output S1_prime
);

  xor xor_1 (S1_prime, S0, S1);
endmodule

module cnt_S0 (
  input  S1,
  input  S0,
  input  TA,
  input  TB,
  output S0_prime
);

  wire and_1_out, and_2_out, not_1_out, not_2_out, not_3_out, not_4_out;

  not not_1 (not_1_out, S1);
  not not_2 (not_2_out, S0);
  not not_3 (not_3_out, TA);
  not not_4 (not_4_out, TB);
  and and_1 (and_1_out, not_1_out, not_2_out, not_3_out);
  and and_2 (and_2_out, not_2_out, S1, not_4_out);
  or or_1 (S0_prime, and_1_out, and_2_out);
endmodule
