// Logisim project 单周期CPU_after_class.circ as structural Verilog: 10 circuits, main circuit main
module main (
  input  in_1,
  output [31:0] out_2,
  output [31:0] out_3,
  output out_4,
  output [4:0] out_5,
  output [31:0] out_6,
  output out_7,
  output [31:0] out_8,
  output [31:0] out_9
);

  wire BSel, clk, extOp, zero;
  wire [2:0] ALUOp, npcOp, WDSel, wrA3Sel;
  wire [31:0] dm_1_rd, ext_1_extend, grf_1_rd1, multiplexer_3_out, npc_1_npc, PC_4;

  NPC npc_1 (.PC(out_3), .IMM(out_2[25:0]), .zero(zero), .NPCOp(npcOp), .NPC(npc_1_npc), .ra(grf_1_rd1), .PC_4(PC_4));
  Clock clock_1 (.out(clk));
  // Probe on out_2[31:26]
  // Probe on out_2[5:0]
  IFU ifu_1 (.clk(clk), .reset(in_1), .NPC(npc_1_npc), .instruct(out_2), .PC(out_3));
  Multiplexer #(.select(3), .width(5)) multiplexer_1 (
    .in0(out_2[20:16]), .in1(out_2[15:11]), .in2({5{1'b1}}), .out(out_5), .sel(wrA3Sel));  // open: in3, in4, in5, in6, in7, en
  Multiplexer #(.select(3), .width(32)) multiplexer_2 (
    .in0(out_8), .in1(dm_1_rd), .in2(PC_4), .out(out_6), .sel(WDSel));  // open: in3, in4, in5, in6, in7, en
  CTRL ctrl_1 (
    .OPcode(out_2[31:26]), .Funccode(out_2[5:0]), .NPCOp(npcOp), .wrA3Sel(wrA3Sel), .WDSel(WDSel),
    .BSel(BSel), .DMWR(out_7), .extOp(extOp), .ALUOp(ALUOp), .weSel(out_4));
  EXT ext_1 (.IMM(out_2[15:0]), .EXTOp(extOp), .extend(ext_1_extend));
  GRF grf_1 (
    .clk(clk), .reset(in_1), .WD(out_6), .WE(out_4), .A3(out_5), .A1(out_2[25:21]), .A2(out_2[20:16]),
    .RD1(grf_1_rd1), .RD2(out_9));
  Multiplexer #(.width(32)) multiplexer_3 (
    .in0(out_9), .in1(ext_1_extend), .out(multiplexer_3_out), .sel(BSel));  // open: en
  ALU alu_1 (.A(grf_1_rd1), .B(multiplexer_3_out), .ALUopcode(ALUOp), .zero(zero), .C(out_8), .in_4(out_2[10:6]));
  DM dm_1 (.addr(out_8), .WD(out_9), .clk(clk), .reset(in_1), .wr(out_7), .RD(dm_1_rd));

  // Other names for the same wires on the sheet: Instr[31:0] = out_2; shamt[4:0] = out_2[10:6]; MemAddr[31:0] = out_8;
  //   MemData[31:0] = out_9; pc[31:0] = out_3; RegAddr[4:0] = out_5; RegData[31:0] = out_6; reset = in_1;
  //   RegWrite = out_4; weSel = out_4; MemWrite = out_7; WR = out_7

  // Notes on the sheet:
  //   addr $rd
  //   addr $rs
  //   addr $rt
  //   $rt
  //   $rs
endmodule

module IFU (
  input  clk,
  input  reset,
  input  [31:0] NPC,
  output [31:0] instruct,
  output [31:0] PC
);

  wire comparator_1_eq;
  wire [31:0] register_1_q, subtractor_1_out;

  Register #(.width(32)) register_1 (.D(NPC), .Q(register_1_q), .clk(clk), .clr(reset));  // open: en
  Comparator #(.width(32), .mode("unsigned")) comparator_1 (
    .a(register_1_q), .b({32{1'b0}}), .eq(comparator_1_eq));  // open: gt, lt
  Multiplexer #(.width(32)) multiplexer_1 (
    .in0(register_1_q), .in1(32'h3000), .out(PC), .sel(comparator_1_eq));  // open: en
  Subtractor #(.width(32)) subtractor_1 (.a(PC), .b(32'h3000), .out(subtractor_1_out));  // open: bin, bout
  ROM #(.addrWidth(12), .dataWidth(32)) rom_1 (.addr(subtractor_1_out[13:2]), .data(instruct));  // open: sel

  // Notes on the sheet:
  //   contents of rom_1 (hex, n*v repeats v):
  //   34210014 ac010000 8c020000 8c030000 8c040000 8c050000 8c060000
endmodule

module GRF (
  input  clk,
  input  reset,
  input  [31:0] WD,
  input  WE,
  input  [4:0] A3,
  input  [4:0] A1,
  input  [4:0] A2,
  output [31:0] RD1,
  output [31:0] RD2
);

  wire [31:0] _0, _1, _2, _3, _4, _5, _6, _7, _8, _9, _10, _11, _12, _13, _14, _15, _16, _17, _18, _19, _20,
       _21, _22, _23, _24, _25, _26, _27, _28, _29, _30, _31, demultiplexer_1_out1, demultiplexer_1_out2,
       demultiplexer_1_out3, demultiplexer_1_out4, demultiplexer_1_out5, demultiplexer_1_out6,
       demultiplexer_1_out7, demultiplexer_1_out8, demultiplexer_1_out9, demultiplexer_1_out10,
       demultiplexer_1_out11, demultiplexer_1_out12, demultiplexer_1_out13, demultiplexer_1_out14,
       demultiplexer_1_out15, demultiplexer_1_out16, demultiplexer_1_out17, demultiplexer_1_out18,
       demultiplexer_1_out19, demultiplexer_1_out20, demultiplexer_1_out21, demultiplexer_1_out22,
       demultiplexer_1_out23, demultiplexer_1_out24, demultiplexer_1_out25, demultiplexer_1_out26,
       demultiplexer_1_out27, demultiplexer_1_out28, demultiplexer_1_out29, demultiplexer_1_out30,
       demultiplexer_1_out31;

  Demultiplexer #(.select(5), .width(32), .tristate("true")) demultiplexer_1 (
    .out1(demultiplexer_1_out1), .out2(demultiplexer_1_out2), .out3(demultiplexer_1_out3),
    .out4(demultiplexer_1_out4), .out5(demultiplexer_1_out5), .out6(demultiplexer_1_out6),
    .out7(demultiplexer_1_out7), .out8(demultiplexer_1_out8), .out9(demultiplexer_1_out9),
    .out10(demultiplexer_1_out10), .out11(demultiplexer_1_out11), .out12(demultiplexer_1_out12),
    .out13(demultiplexer_1_out13), .out14(demultiplexer_1_out14), .out15(demultiplexer_1_out15),
    .out16(demultiplexer_1_out16), .out17(demultiplexer_1_out17), .out18(demultiplexer_1_out18),
    .out19(demultiplexer_1_out19), .out20(demultiplexer_1_out20), .out21(demultiplexer_1_out21),
    .out22(demultiplexer_1_out22), .out23(demultiplexer_1_out23), .out24(demultiplexer_1_out24),
    .out25(demultiplexer_1_out25), .out26(demultiplexer_1_out26), .out27(demultiplexer_1_out27),
    .out28(demultiplexer_1_out28), .out29(demultiplexer_1_out29), .out30(demultiplexer_1_out30),
    .out31(demultiplexer_1_out31), .in(WD), .sel(A3), .en(WE));  // open: out0
  Register #(.width(32)) u__0 (.D({32{1'b0}}), .Q(_0), .clk(clk), .clr(reset));  // open: en
  Register #(.width(32)) u__1 (.D(demultiplexer_1_out1), .Q(_1), .clk(clk), .clr(reset));  // open: en
  Register #(.width(32)) _1_2 (.D(demultiplexer_1_out2), .Q(_2), .clk(clk), .clr(reset));  // open: en
  Register #(.width(32)) _1_3 (.D(demultiplexer_1_out3), .Q(_3), .clk(clk), .clr(reset));  // open: en
  Register #(.width(32)) _1_4 (.D(demultiplexer_1_out4), .Q(_4), .clk(clk), .clr(reset));  // open: en
  Register #(.width(32)) _1_5 (.D(demultiplexer_1_out5), .Q(_5), .clk(clk), .clr(reset));  // open: en
  Register #(.width(32)) _1_6 (.D(demultiplexer_1_out6), .Q(_6), .clk(clk), .clr(reset));  // open: en
  Register #(.width(32)) _1_7 (.D(demultiplexer_1_out7), .Q(_7), .clk(clk), .clr(reset));  // open: en
  Register #(.width(32)) _1_8 (.D(demultiplexer_1_out9), .Q(_9), .clk(clk), .clr(reset));  // open: en
  Register #(.width(32)) _1_9 (.D(demultiplexer_1_out10), .Q(_10), .clk(clk), .clr(reset));  // open: en
  Register #(.width(32)) _1_10 (.D(demultiplexer_1_out11), .Q(_11), .clk(clk), .clr(reset));  // open: en
  Register #(.width(32)) _1_11 (.D(demultiplexer_1_out12), .Q(_12), .clk(clk), .clr(reset));  // open: en
  Register #(.width(32)) _1_12 (.D(demultiplexer_1_out13), .Q(_13), .clk(clk), .clr(reset));  // open: en
  Register #(.width(32)) _1_13 (.D(demultiplexer_1_out14), .Q(_14), .clk(clk), .clr(reset));  // open: en
  Register #(.width(32)) _1_14 (.D(demultiplexer_1_out15), .Q(_15), .clk(clk), .clr(reset));  // open: en
  Register #(.width(32)) _1_15 (.D(demultiplexer_1_out16), .Q(_16), .clk(clk), .clr(reset));  // open: en
  Register #(.width(32)) _1_16 (.D(demultiplexer_1_out17), .Q(_17), .clk(clk), .clr(reset));  // open: en
  Register #(.width(32)) _1_17 (.D(demultiplexer_1_out18), .Q(_18), .clk(clk), .clr(reset));  // open: en
  Register #(.width(32)) _1_18 (.D(demultiplexer_1_out19), .Q(_19), .clk(clk), .clr(reset));  // open: en
  Register #(.width(32)) _1_19 (.D(demultiplexer_1_out20), .Q(_20), .clk(clk), .clr(reset));  // open: en
  Register #(.width(32)) _1_20 (.D(demultiplexer_1_out21), .Q(_21), .clk(clk), .clr(reset));  // open: en
  Register #(.width(32)) _1_21 (.D(demultiplexer_1_out22), .Q(_22), .clk(clk), .clr(reset));  // open: en
  Register #(.width(32)) _1_22 (.D(demultiplexer_1_out23), .Q(_23), .clk(clk), .clr(reset));  // open: en
  Register #(.width(32)) _1_23 (.D(demultiplexer_1_out24), .Q(_24), .clk(clk), .clr(reset));  // open: en
  Register #(.width(32)) _1_24 (.D(demultiplexer_1_out25), .Q(_25), .clk(clk), .clr(reset));  // open: en
  Register #(.width(32)) _1_25 (.D(demultiplexer_1_out26), .Q(_26), .clk(clk), .clr(reset));  // open: en
  Register #(.width(32)) _1_26 (.D(demultiplexer_1_out27), .Q(_27), .clk(clk), .clr(reset));  // open: en
  Register #(.width(32)) _1_27 (.D(demultiplexer_1_out28), .Q(_28), .clk(clk), .clr(reset));  // open: en
  Register #(.width(32)) _1_28 (.D(demultiplexer_1_out29), .Q(_29), .clk(clk), .clr(reset));  // open: en
  Register #(.width(32)) _1_29 (.D(demultiplexer_1_out30), .Q(_30), .clk(clk), .clr(reset));  // open: en
  Register #(.width(32)) _1_30 (.D(demultiplexer_1_out31), .Q(_31), .clk(clk), .clr(reset));  // open: en
  Register #(.width(32)) _1_31 (.D(demultiplexer_1_out8), .Q(_8), .clk(clk), .clr(reset));  // open: en
  Multiplexer #(.select(5), .width(32)) multiplexer_1 (
    .in0(_0), .in1(_1), .in2(_2), .in3(_3), .in4(_4), .in5(_5), .in6(_6), .in7(_7), .in8(_8), .in9(_9),
    .in10(_10), .in11(_11), .in12(_12), .in13(_13), .in14(_14), .in15(_15), .in16(_16), .in17(_17),
    .in18(_18), .in19(_19), .in20(_20), .in21(_21), .in22(_22), .in23(_23), .in24(_24), .in25(_25),
    .in26(_26), .in27(_27), .in28(_28), .in29(_29), .in30(_30), .in31(_31), .out(RD1), .sel(A1));  // open: en
  Multiplexer #(.select(5), .width(32)) multiplexer_2 (
    .in0(_0), .in1(_1), .in2(_2), .in3(_3), .in4(_4), .in5(_5), .in6(_6), .in7(_7), .in8(_8), .in9(_9),
    .in10(_10), .in11(_11), .in12(_12), .in13(_13), .in14(_14), .in15(_15), .in16(_16), .in17(_17),
    .in18(_18), .in19(_19), .in20(_20), .in21(_21), .in22(_22), .in23(_23), .in24(_24), .in25(_25),
    .in26(_26), .in27(_27), .in28(_28), .in29(_29), .in30(_30), .in31(_31), .out(RD2), .sel(A2));  // open: en

  // Notes on the sheet:
  //   而不是地址
  //   GRF本身就在操作寄存器
endmodule

module ALU (
  input  [31:0] A,
  input  [31:0] B,
  input  [2:0] ALUopcode,
  input  [4:0] in_4,
  output zero,
  output [31:0] C
);

  wire [31:0] add, \or , sll, sub;

  Shifter #(.width(32)) shifter_1 (.in(B), .\dist (in_4), .out(sll));
  Adder #(.width(32)) adder_1 (.a(A), .b(B), .out(add));  // open: cin, cout
  Subtractor #(.width(32)) subtractor_1 (.a(A), .b(B), .out(sub));  // open: bin, bout
  assign \or  = A | B;  // OR_Gate or_1, 32 bits wide
  Comparator #(.width(32)) comparator_1 (.a(A), .b(B), .eq(zero));  // open: gt, lt
  Multiplexer #(.select(3), .width(32)) multiplexer_1 (
    .in0(add), .in1(sub), .in2(\or ), .in3({B[15:0], {16{1'b0}}}), .in4(sll), .out(C), .sel(ALUopcode));  // open: in5, in6, in7, en

  // Other names for the same wires on the sheet: lui[31:16] = B[15:0]
endmodule

module DM (
  input  [31:0] addr,
  input  [31:0] WD,
  input  clk,
  input  reset,
  input  wr,
  output [31:0] RD
);

  RAM #(.addrWidth(12), .dataWidth(32), .bus("separate")) ram_1 (
    .addr(addr[13:2]), .din(WD), .data(RD), .str(wr), .clk(clk), .clr(reset));  // open: sel, ld
endmodule

module EXT (
  input  [15:0] IMM,
  input  EXTOp,
  output [31:0] extend
);

  wire [31:0] bit_extender_1_out, bit_extender_2_out;

  assign bit_extender_1_out = {{16{1'b0}}, IMM};  // Bit_Extender bit_extender_1
  assign bit_extender_2_out = {{16{IMM[15]}}, IMM};  // Bit_Extender bit_extender_2
  Multiplexer #(.width(32)) multiplexer_1 (
    .in0(bit_extender_1_out), .in1(bit_extender_2_out), .out(extend), .sel(EXTOp));  // open: en
endmodule

module NPC (
  input  [31:0] PC,
  input  zero,
  input  [25:0] IMM,
  input  [2:0] NPCOp,
  input  [31:0] ra,
  output [31:0] PC_4,
  output [31:0] NPC
);

  wire [31:0] beq, bit_extender_1_out, multiplexer_1_out;

  assign bit_extender_1_out = {{14{IMM[15]}}, {IMM[15:0], 2'b00}};  // Bit_Extender bit_extender_1
  Adder #(.width(32)) adder_1 (.a(PC), .b(32'h4), .out(PC_4));  // open: cin, cout
  Adder #(.width(32)) adder_2 (.a(PC_4), .b(bit_extender_1_out), .out(beq));  // open: cin, cout
  Multiplexer #(.width(32)) multiplexer_1 (.in0(PC_4), .in1(beq), .out(multiplexer_1_out), .sel(zero));  // open: en
  Multiplexer #(.select(3), .width(32)) multiplexer_2 (
    .in0(PC_4), .in1(multiplexer_1_out), .in2({PC[31:28], IMM, 2'b00}), .in3(ra), .out(NPC), .sel(NPCOp));  // open: in4, in5, in6, in7, en

  // Notes on the sheet:
  //   beq
  //   j
  //   jal
  //   jalr
  //   jr
  //   010
  //   011
endmodule

module CTRL (
  input  [5:0] Funccode,
  input  [5:0] OPcode,
  output [2:0] NPCOp,
  output [2:0] WDSel,
  output BSel,
  output DMWR,
  output extOp,
  output weSel,
  output [2:0] wrA3Sel,
  output [2:0] ALUOp
);

  wire add_out, beq_out, j_out, jal_out, jalr_out, jr_out, lui_out, lw_out, not_1_out, not_2_out, not_3_out,
       not_4_out, not_5_out, not_6_out, not_7_out, not_8_out, not_9_out, not_10_out, not_11_out, not_12_out,
       ori_out, sll_out, special_out, sub_out, sw_out;

  not not_1 (not_1_out, OPcode[5]);
  not not_2 (not_2_out, OPcode[4]);
  not not_3 (not_3_out, OPcode[3]);
  not not_4 (not_4_out, OPcode[2]);
  not not_5 (not_5_out, OPcode[1]);
  not not_6 (not_6_out, OPcode[0]);
  not not_7 (not_7_out, Funccode[5]);
  not not_8 (not_8_out, Funccode[4]);
  not not_9 (not_9_out, Funccode[3]);
  not not_10 (not_10_out, Funccode[2]);
  not not_11 (not_11_out, Funccode[1]);
  not not_12 (not_12_out, Funccode[0]);
  and special (special_out, not_1_out, not_2_out, not_3_out, not_4_out, not_5_out, not_6_out);
  and add (add_out, Funccode[5], not_8_out, not_9_out, special_out, not_10_out, not_11_out, not_12_out);
  and sub (sub_out, Funccode[5], not_8_out, not_9_out, special_out, not_10_out, Funccode[1], not_12_out);
  and ori (ori_out, not_1_out, not_2_out, OPcode[3], OPcode[2], not_5_out, OPcode[0]);
  and lw (lw_out, OPcode[5], not_2_out, not_3_out, not_4_out, OPcode[1], OPcode[0]);
  and sw (sw_out, OPcode[5], not_2_out, OPcode[3], not_4_out, OPcode[1], OPcode[0]);
  and beq (beq_out, not_1_out, not_2_out, not_3_out, OPcode[2], not_5_out, not_6_out);
  and lui (lui_out, not_1_out, not_2_out, OPcode[3], OPcode[2], OPcode[1], OPcode[0]);
  and sll (sll_out, not_1_out, not_2_out, not_3_out, not_4_out, not_5_out, not_6_out, not_7_out, not_8_out, not_9_out, not_10_out, not_11_out, not_12_out);
  and j (j_out, not_1_out, not_2_out, not_3_out, not_4_out, OPcode[1], not_6_out);
  and jal (jal_out, not_1_out, not_2_out, not_3_out, not_4_out, OPcode[1], OPcode[0]);
  and jalr (jalr_out, not_7_out, not_8_out, Funccode[3], special_out, not_10_out, not_11_out, Funccode[0]);
  and jr (jr_out, not_7_out, not_8_out, Funccode[3], special_out, not_10_out, not_11_out, not_12_out);
  buf or_1 (NPCOp[2], 1'b0);  // OR_Gate
  or or_2 (NPCOp[0], beq_out, jr_out, jalr_out);
  or or_3 (NPCOp[1], jr_out, j_out, jal_out, jalr_out);
  buf or_4 (wrA3Sel[2], 1'b0);  // OR_Gate
  buf or_5 (wrA3Sel[1], jal_out);  // OR_Gate
  or or_6 (wrA3Sel[0], add_out, sub_out, sll_out);
  buf or_7 (WDSel[2], 1'b0);  // OR_Gate
  or or_8 (WDSel[1], jalr_out, jal_out);
  or or_9 (WDSel[0], lw_out, 1'b0);
  or or_10 (BSel, lw_out, ori_out, sw_out, lui_out);
  buf or_11 (DMWR, sw_out);  // OR_Gate
  or or_12 (extOp, lw_out, sw_out);
  buf or_13 (ALUOp[2], sll_out);  // OR_Gate
  or or_14 (ALUOp[1], ori_out, lui_out);
  or or_15 (ALUOp[0], lui_out, beq_out, sub_out);
  or or_16 (weSel, jalr_out, sll_out, ori_out, lw_out, sub_out, lui_out, add_out, jal_out);

  // Notes on the sheet:
  //   001101
  //   100011
  //   101011
  //   000100
  //   001111
  //   000010
  //   000011
  //   001001
  //   001000
  //   想写入就得enable
endmodule

module reverse (
  input  [31:0] in_1,
  output [31:0] out_2
);


  assign out_2 = {in_1[0], in_1[1], in_1[2], in_1[3], in_1[4], in_1[5], in_1[6], in_1[7], in_1[8], in_1[9], in_1[10], in_1[11], in_1[12], in_1[13], in_1[14], in_1[15], in_1[16], in_1[17], in_1[18], in_1[19], in_1[20], in_1[21], in_1[22], in_1[23], in_1[24], in_1[25], in_1[26], in_1[27], in_1[28], in_1[29], in_1[30], in_1[31]};
endmodule

module LWF (
  input  [31:0] offset,
  input  [31:0] rt,
  output out_3
);

  wire [5:1] bitadder_1_out;
  wire [31:0] and_1_out;

  assign and_1_out = offset & rt;  // AND_Gate and_1, 32 bits wide
  BitAdder #(.width(32)) bitadder_1 (.in0(and_1_out), .out({bitadder_1_out, out_3}));

  // Notes on the sheet:
  //   确认时计数还是偶数看最后一位
  //   1奇0偶
endmodule
