// Logisim project 单周期CPU_in_class.circ as structural Verilog: 10 circuits, main circuit main
module main (
  input  in_1,
  output [31:0] out_2,
  output [31:0] out_3,
  output out_4,
  output [4:0] out_5,
  output [31:0] out_6,
  output out_7,
  output [31:0] out_8,
  output [31:0] out_9
);

  wire BSel, clk, extOp, odd_or_even, tunnel, tunnel_t, zero;
  wire [2:0] npcOp, WDSel, wrA3Sel;
  wire [3:0] ALUOp;
  wire [4:0] adder_1_out;
  wire [31:0] dm_1_rd, ext_1_extend, grf_1_rd1, multiplexer_3_out, npc_1_npc, PC_4, tmp1, tmp2;

  NPC npc_1 (
    .PC(out_3), .IMM(out_2[25:0]), .zero(zero), .NPCOp(npcOp), .NPC(npc_1_npc), .ra(grf_1_rd1), .PC_4(PC_4),
    .in_6(tunnel));
  Clock clock_1 (.out(clk));
  // Probe on out_2[31:26]
  // Probe on out_2[5:0]
  IFU ifu_1 (.clk(clk), .reset(in_1), .NPC(npc_1_npc), .instruct(out_2), .PC(out_3));
  Adder #(.width(5)) adder_1 (.a(out_2[20:16]), .b(5'b00001), .out(adder_1_out));  // open: cin, cout
  Multiplexer #(.select(3), .width(5)) multiplexer_1 (
    .in0(out_2[20:16]), .in1(out_2[15:11]), .in2({5{1'b1}}), .in3(out_2[25:21]), .in4(adder_1_out),
    .out(out_5), .sel(wrA3Sel));  // open: in5, in6, in7, en
  Multiplexer #(.select(3), .width(32)) multiplexer_2 (
    .in0(out_8), .in1(dm_1_rd), .in2(PC_4), .in3(tmp1), .in4(tmp2), .out(out_6), .sel(WDSel));  // open: in5, in6, in7, en
  CTRL ctrl_1 (
    .OPcode(out_2[31:26]), .Funccode(out_2[5:0]), .NPCOp(npcOp), .wrA3Sel(wrA3Sel), .WDSel(WDSel),
    .BSel(BSel), .DMWR(out_7), .extOp(extOp), .ALUOp(ALUOp), .weSel(out_4), .in_2(tunnel), .in_1(tunnel_t),
    .in_3(odd_or_even));
  EXT ext_1 (.IMM(out_2[15:0]), .EXTOp(extOp), .extend(ext_1_extend));
  GRF grf_1 (
    .clk(clk), .reset(in_1), .WD(out_6), .WE(out_4), .A3(out_5), .A1(out_2[25:21]), .A2(out_2[20:16]),
    .RD1(grf_1_rd1), .RD2(out_9));
  Multiplexer #(.width(32)) multiplexer_3 (
    .in0(out_9), .in1(ext_1_extend), .out(multiplexer_3_out), .sel(BSel));  // open: en
  ALU alu_1 (
    .A(grf_1_rd1), .B(multiplexer_3_out), .ALUopcode(ALUOp), .zero(zero), .C(out_8), .in_4(out_2[10:6]),
    .tmp1(tmp1), .tmp2(tmp2), .out_7(tunnel), .out_9(tunnel_t));
  LWF lwf_1 (.offset(dm_1_rd), .rt(out_9), .out_3(odd_or_even));
  DM dm_1 (.addr(out_8), .WD(out_9), .clk(clk), .reset(in_1), .wr(out_7), .RD(dm_1_rd));

  // Other names for the same wires on the sheet: Instr[31:0] = out_2; shamt[4:0] = out_2[10:6]; MemAddr[31:0] = out_8;
  //   pc[31:0] = out_3; RegAddr[4:0] = out_5; RegData[31:0] = out_6; reset = in_1; MemData[31:0] = out_9;
  //   rt[31:0] = out_9; RegWrite = out_4; weSel = out_4; MemWrite = out_7; WR = out_7

  // Notes on the sheet:
  //   addr $rd
  //   addr $rs
  //   addr $rt
  //   $rt
  //   $rs
endmodule

module IFU (
  input  clk,
  input  reset,
  input  [31:0] NPC,
  output [31:0] instruct,
  output [31:0] PC
);

  wire comparator_1_eq;
  wire [31:0] register_1_q, subtractor_1_out;

  Register #(.width(32)) register_1 (.D(NPC), .Q(register_1_q), .clk(clk), .clr(reset));  // open: en
  Comparator #(.width(32), .mode("unsigned")) comparator_1 (
    .a(register_1_q), .b({32{1'b0}}), .eq(comparator_1_eq));  // open: gt, lt
  Multiplexer #(.width(32)) multiplexer_1 (
    .in0(register_1_q), .in1(32'h3000), .out(PC), .sel(comparator_1_eq));  // open: en
  Subtractor #(.width(32)) subtractor_1 (.a(PC), .b(32'h3000), .out(subtractor_1_out));  // open: bin, bout
  ROM #(.addrWidth(12), .dataWidth(32)) rom_1 (.addr(subtractor_1_out[13:2]), .data(instruct));  // open: sel

  // Notes on the sheet:
  //   contents of rom_1 (hex, n*v repeats v):
  //   ac190ac8 8c111860 257f823 2407820 ac042a78 3513cdc0 2b42020 8c0628dc 8c030ca4 8c0b2830 2f89823
  //   ac162d68 8c0b1b00 37088df6 3c019aac 8c171374 ac110f94 8c0601bc 23cd820 ac070594 22c9023 8c1d0358
  //   3c12961f 362234d9 31020 3b91020 ac0418ac 36408eda 3c1e12b3 1720823 ac1e0778 ac062e54 8c191ee4
  //   1cc2023 f81820 8c09169c 8c172c70 8c1c0a00 36ca12e5 16f0820 13b7020 3c1c5ed2 36132ffe 8c1b1f54
  //   3443020 342b820 a7e020 35421d43 36511551 3c0a820 350c66b2 1bb3820 37e591e0 ac1803f8 35e9f908 20c8023
  //   37f02add 3c09ec14 30e0023 8c0f133c 3c12c38b ac1e2320 3642549e 2127820 34c6afc3 1d87020 2564023
  //   8c0904dc ac150ee0 19f3023 1f19820 8c182010 8c001e9c 8c0a0b14 2b19023 8c130eb4 ac1e0148 11ef023
  //   1ed2823 24bc023 3294020 ac162fac 8c192d64 3c1939ba 8c1015e8 398e023 8c0b1d80 3573a985 2616023
  //   ac1309e0 3c126229 3c1ffdf6 8c14186c 3605bbb0 8c1601dc 2c70023 1eb5823 cdf820 8c021a88 119020
  //   8c132a88 ac190654 e49820 3c0193c7 8c0d0974 ac120e78 2897820 1a2a023 23bd023 3c0ef332 ac1f032c
  //   3594023 ac18173c 8c091d28 35bf6aa8 42d020 3c006687 ac001564 3422820 8c0e2800 ac131864 ac142040
  //   8c1c0e04 8c1b2f08 24a0023 1188820 3c095274 297d823 ac0c240c ac0d0164 342ce1e9 34eab4fc ac082300
  //   111d820 ac010bec 3a06020 ac1e0f4c 8c11280c 3c0c24f5 37801df0 37f887f4 ac03299c 3c1302d0 3c0333f3
  //   36cd5a5b 34883d01 37cb020 37f3820 ac181ae8 8c161e34 3696009a a9020 34a4e7c0 36c7020 2c45020 3570a705
  //   8c1e2e4c 37a33f05 8c072e08 1599020 21d4823 372acee0 35375abb 8c011cbc 34b644c2 8c1a29b0 3701fb27
  //   ac1615a8 37d1c7c5 8c1120b0 3625bf76 317c020 3419cdc5 3c04f88e 3638023 8c192a3c ac171d9c 35ab020
  //   35b7023 ac052dd8 8c102e84 8c180fac 1e63823 3baf020 926823 ac082b28 ac1f1428 ac1a2fa8 ac160bf0
  //   3c1ccef2 3c066cb1 370d023 36036dc6 8c141c6c ac1a0d64 ac022c98 2f18020 3c1723e4 37f67770 3c04fa3e
  //   ac0a0bec ac1c2014 102f820 174b023 3477023 ac1006cc 7a0820 3c1db717 8c1d25a0 38f9820 372854b6 3b7823
  //   8c092c88 178d023 3c087575 8c11123c 33fb820 3c1692da 15ba823 3a6e823 319d020 ac181fd0 3517af4e
  //   ac1e21e8 1b27023 8c0324e0 34d7e628 eea823 3c0d6cd7 ac071538 8c0c029c ac012dc0 8c0d08dc 8c0b069c
  //   2ba8023 191b820 1ca4020 142d820 8c060200 8c181328 1ba4023 8c1a014c 2614023 dfb823 b95820 8c07098c
  //   3c02ce56 ac022a5c 8c160db4 ac021820 37db0207 3a0a820 36039f13 3578ab88 53b023 3c15f985 8c110770
  //   3979023 ac190da0 3c02baaa 38b7023 3493afe3 ed2820 29a7820 3c0c08b5 1dd7023 3c039317 ac0d0070
  //   3c177d98 3c03e8f6 8c14259c 3c009837 3f81020 3c04ca6f 1609020 ac0d0ca8 370c7563 3c1ff8a5 141c823
  //   8c141dd0 3620480c ac010520 379c992c b78023 8c122998 c18823 3c0c1b87 3c1a4847 8c092174 ac081cb8
  //   3c1ad411 3c0d4f38 ac1e22f8 3774c5c9 3c00e682 ac092f58 398a823 36dcd8bf 1de0023 8c1c095c 3404feda
  //   8c162f64 1a2e820 3ca0020 8c03258c 3c103fdf 8c170258 3c051faf 8c0b2e08 37550512 120b823 ac111194
  //   3c19e0aa ac1312c0 1a08020 8c0e0c64 37d39a8b 386b823 ac0c1e28 8c1a10cc 3700d2b8 3c10a1d3 34e11b4e
  //   3372820 3bf4020 8c180184 8c16046c 124b020 3c005426 36427266 35281f0c 1f57823 ac032cb8 277b023
  //   29d7820 d1e020 36dc4ae6 2be3820 354f820 3c15bbea 3c0a350e 8c0a2124 2be8020 13e8023 8c0e1da0 43d023
  //   332020 ac101f50 369a6207 ac0f0204 8c0a0848 3c00fa84 8c1c2e0c 8c1c1824 8c0d0c0c 103d820 3c149322
  //   3631c2ce 8c0d2cb4 263b023 376bd350 8c060e98 34413782 2369823 ac002db4 352de948 3c11ba1a ac042a10
  //   ac0e0f70 3c1ddd00 292e023 13a4023 8c042530 1bbf820 3d93020 3c0242cb 38c0020 8c152ec8 8c0b2624
  //   3c0a9bc0 3776ee79 1cb4823 8c151d50 ac162af4 3c1ce0c8 3c0d15e4 3c14018e 2151823 ac1911d0 ac001e8c
  //   ac1e0de0 8c082524 1fd6020 80a823 3c025684 36617896 8c0f12e8 ac17233c 857820 29b823 ac061a40 2e1c020
  //   3c190d23 351af189 3ac3020 37989436 25f7823 3c67820 3539b7c6 8c1915dc ac1906e4 8c040db4 3c175fd0
  //   374ecb23 2e16020 8c0b1940 8c0e0310 151b023 8c0e29ac 3c0df345 ee1820 3461cc40 379d823 69c023 ac090418
  //   27fa020 ac1d26d0 3c14023 3c18ca18 8c0a1b58 346557f4 ac030360 d11823 2cb2823 b8823 3c1c9f4f 3118823
  //   8c0f2008 162023 2bf3023 35d842e3 33b023 ac1415e8 21c6820 352c023 43b023 ac120854 3c187b86 245b820
  //   3c1b568a 182c020 8c0107d4 3c1726db 3794d055 3c1c1026 34fdec7d 3b0f020 8c000afc 8c1f1190 428823
  //   3869020 16bd820 1d0e823 8c1f0b40 8c061484 ac1712d0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
endmodule

module GRF (
  input  clk,
  input  reset,
  input  [31:0] WD,
  input  WE,
  input  [4:0] A3,
  input  [4:0] A1,
  input  [4:0] A2,
  output [31:0] RD1,
  output [31:0] RD2
);

  wire [31:0] _0, _1, _2, _3, _4, _5, _6, _7, _8, _9, _10, _11, _12, _13, _14, _15, _16, _17, _18, _19, _20,
       _21, _22, _23, _24, _25, _26, _27, _28, _29, _30, _31, demultiplexer_1_out1, demultiplexer_1_out2,
       demultiplexer_1_out3, demultiplexer_1_out4, demultiplexer_1_out5, demultiplexer_1_out6,
       demultiplexer_1_out7, demultiplexer_1_out8, demultiplexer_1_out9, demultiplexer_1_out10,
       demultiplexer_1_out11, demultiplexer_1_out12, demultiplexer_1_out13, demultiplexer_1_out14,
       demultiplexer_1_out15, demultiplexer_1_out16, demultiplexer_1_out17, demultiplexer_1_out18,
       demultiplexer_1_out19, demultiplexer_1_out20, demultiplexer_1_out21, demultiplexer_1_out22,
       demultiplexer_1_out23, demultiplexer_1_out24, demultiplexer_1_out25, demultiplexer_1_out26,
       demultiplexer_1_out27, demultiplexer_1_out28, demultiplexer_1_out29, demultiplexer_1_out30,
       demultiplexer_1_out31;

  Demultiplexer #(.select(5), .width(32), .tristate("true")) demultiplexer_1 (
    .out1(demultiplexer_1_out1), .out2(demultiplexer_1_out2), .out3(demultiplexer_1_out3),
    .out4(demultiplexer_1_out4), .out5(demultiplexer_1_out5), .out6(demultiplexer_1_out6),
    .out7(demultiplexer_1_out7), .out8(demultiplexer_1_out8), .out9(demultiplexer_1_out9),
    .out10(demultiplexer_1_out10), .out11(demultiplexer_1_out11), .out12(demultiplexer_1_out12),
    .out13(demultiplexer_1_out13), .out14(demultiplexer_1_out14), .out15(demultiplexer_1_out15),
    .out16(demultiplexer_1_out16), .out17(demultiplexer_1_out17), .out18(demultiplexer_1_out18),
    .out19(demultiplexer_1_out19), .out20(demultiplexer_1_out20), .out21(demultiplexer_1_out21),
    .out22(demultiplexer_1_out22), .out23(demultiplexer_1_out23), .out24(demultiplexer_1_out24),
    .out25(demultiplexer_1_out25), .out26(demultiplexer_1_out26), .out27(demultiplexer_1_out27),
    .out28(demultiplexer_1_out28), .out29(demultiplexer_1_out29), .out30(demultiplexer_1_out30),
    .out31(demultiplexer_1_out31), .in(WD), .sel(A3), .en(WE));  // open: out0
  Register #(.width(32)) u__0 (.D({32{1'b0}}), .Q(_0), .clk(clk), .clr(reset));  // open: en
  Register #(.width(32)) u__1 (.D(demultiplexer_1_out1), .Q(_1), .clk(clk), .clr(reset));  // open: en
  Register #(.width(32)) _1_2 (.D(demultiplexer_1_out2), .Q(_2), .clk(clk), .clr(reset));  // open: en
  Register #(.width(32)) _1_3 (.D(demultiplexer_1_out3), .Q(_3), .clk(clk), .clr(reset));  // open: en
  Register #(.width(32)) _1_4 (.D(demultiplexer_1_out4), .Q(_4), .clk(clk), .clr(reset));  // open: en
  Register #(.width(32)) _1_5 (.D(demultiplexer_1_out5), .Q(_5), .clk(clk), .clr(reset));  // open: en
  Register #(.width(32)) _1_6 (.D(demultiplexer_1_out6), .Q(_6), .clk(clk), .clr(reset));  // open: en
  Register #(.width(32)) _1_7 (.D(demultiplexer_1_out7), .Q(_7), .clk(clk), .clr(reset));  // open: en
  Register #(.width(32)) _1_8 (.D(demultiplexer_1_out9), .Q(_9), .clk(clk), .clr(reset));  // open: en
  Register #(.width(32)) _1_9 (.D(demultiplexer_1_out10), .Q(_10), .clk(clk), .clr(reset));  // open: en
  Register #(.width(32)) _1_10 (.D(demultiplexer_1_out11), .Q(_11), .clk(clk), .clr(reset));  // open: en
  Register #(.width(32)) _1_11 (.D(demultiplexer_1_out12), .Q(_12), .clk(clk), .clr(reset));  // open: en
  Register #(.width(32)) _1_12 (.D(demultiplexer_1_out13), .Q(_13), .clk(clk), .clr(reset));  // open: en
  Register #(.width(32)) _1_13 (.D(demultiplexer_1_out14), .Q(_14), .clk(clk), .clr(reset));  // open: en
  Register #(.width(32)) _1_14 (.D(demultiplexer_1_out15), .Q(_15), .clk(clk), .clr(reset));  // open: en
  Register #(.width(32)) _1_15 (.D(demultiplexer_1_out16), .Q(_16), .clk(clk), .clr(reset));  // open: en
  Register #(.width(32)) _1_16 (.D(demultiplexer_1_out17), .Q(_17), .clk(clk), .clr(reset));  // open: en
  Register #(.width(32)) _1_17 (.D(demultiplexer_1_out18), .Q(_18), .clk(clk), .clr(reset));  // open: en
  Register #(.width(32)) _1_18 (.D(demultiplexer_1_out19), .Q(_19), .clk(clk), .clr(reset));  // open: en
  Register #(.width(32)) _1_19 (.D(demultiplexer_1_out20), .Q(_20), .clk(clk), .clr(reset));  // open: en
  Register #(.width(32)) _1_20 (.D(demultiplexer_1_out21), .Q(_21), .clk(clk), .clr(reset));  // open: en
  Register #(.width(32)) _1_21 (.D(demultiplexer_1_out22), .Q(_22), .clk(clk), .clr(reset));  // open: en
  Register #(.width(32)) _1_22 (.D(demultiplexer_1_out23), .Q(_23), .clk(clk), .clr(reset));  // open: en
  Register #(.width(32)) _1_23 (.D(demultiplexer_1_out24), .Q(_24), .clk(clk), .clr(reset));  // open: en
  Register #(.width(32)) _1_24 (.D(demultiplexer_1_out25), .Q(_25), .clk(clk), .clr(reset));  // open: en
  Register #(.width(32)) _1_25 (.D(demultiplexer_1_out26), .Q(_26), .clk(clk), .clr(reset));  // open: en
  Register #(.width(32)) _1_26 (.D(demultiplexer_1_out27), .Q(_27), .clk(clk), .clr(reset));  // open: en
  Register #(.width(32)) _1_27 (.D(demultiplexer_1_out28), .Q(_28), .clk(clk), .clr(reset));  // open: en
  Register #(.width(32)) _1_28 (.D(demultiplexer_1_out29), .Q(_29), .clk(clk), .clr(reset));  // open: en
  Register #(.width(32)) _1_29 (.D(demultiplexer_1_out30), .Q(_30), .clk(clk), .clr(reset));  // open: en
  Register #(.width(32)) _1_30 (.D(demultiplexer_1_out31), .Q(_31), .clk(clk), .clr(reset));  // open: en
  Register #(.width(32)) _1_31 (.D(demultiplexer_1_out8), .Q(_8), .clk(clk), .clr(reset));  // open: en
  Multiplexer #(.select(5), .width(32)) multiplexer_1 (
    .in0(_0), .in1(_1), .in2(_2), .in3(_3), .in4(_4), .in5(_5), .in6(_6), .in7(_7), .in8(_8), .in9(_9),
    .in10(_10), .in11(_11), .in12(_12), .in13(_13), .in14(_14), .in15(_15), .in16(_16), .in17(_17),
    .in18(_18), .in19(_19), .in20(_20), .in21(_21), .in22(_22), .in23(_23), .in24(_24), .in25(_25),
    .in26(_26), .in27(_27), .in28(_28), .in29(_29), .in30(_30), .in31(_31), .out(RD1), .sel(A1));  // open: en
  Multiplexer #(.select(5), .width(32)) multiplexer_2 (
    .in0(_0), .in1(_1), .in2(_2), .in3(_3), .in4(_4), .in5(_5), .in6(_6), .in7(_7), .in8(_8), .in9(_9),
    .in10(_10), .in11(_11), .in12(_12), .in13(_13), .in14(_14), .in15(_15), .in16(_16), .in17(_17),
    .in18(_18), .in19(_19), .in20(_20), .in21(_21), .in22(_22), .in23(_23), .in24(_24), .in25(_25),
    .in26(_26), .in27(_27), .in28(_28), .in29(_29), .in30(_30), .in31(_31), .out(RD2), .sel(A2));  // open: en

  // Notes on the sheet:
  //   而不是地址
  //   GRF本身就在操作寄存器
endmodule

module ALU (
  input  [31:0] A,
  input  [31:0] B,
  input  [3:0] ALUopcode,
  input  [4:0] in_4,
  output zero,
  output [31:0] C,
  output out_7,
  output [31:0] tmp1,
  output out_9,
  output [31:0] tmp2
);

  wire bitfinder_1_found, bitfinder_2_found;
  wire [4:0] bitfinder_1_index, bitfinder_2_index, subtractor_1_out, subtractor_2_out;
  wire [31:0] add, bit_extender_1_out, bit_extender_2_out, \or , rev, reverse_1_out_2, shifter_2_out,
       shifter_3_out, shifter_4_out, sll, sub, subtractor_3_out;

  Shifter #(.width(32)) shifter_1 (.in(B), .\dist (in_4), .out(sll));
  BitFinder #(.width(32), .\type ("high1")) bitfinder_1 (.in(A), .index(bitfinder_1_index), .found(bitfinder_1_found));
  BitFinder #(.width(32), .\type ("high1")) bitfinder_2 (.in(B), .index(bitfinder_2_index), .found(bitfinder_2_found));
  Adder #(.width(32)) adder_1 (.a(A), .b(B), .out(add));  // open: cin, cout
  Subtractor #(.width(5)) subtractor_1 (
    .a({5{1'b1}}), .b(bitfinder_1_index), .out(subtractor_1_out));  // open: bin, bout
  Subtractor #(.width(5)) subtractor_2 (
    .a({5{1'b1}}), .b(bitfinder_2_index), .out(subtractor_2_out));  // open: bin, bout
  Shifter #(.width(32)) shifter_2 (.in(A), .\dist (B[4:0]), .out(shifter_2_out));
  reverse reverse_1 (.in_1(A), .out_2(reverse_1_out_2));
  assign bit_extender_1_out = {{27{1'b0}}, subtractor_1_out};  // Bit_Extender bit_extender_1
  assign bit_extender_2_out = {{27{1'b0}}, subtractor_2_out};  // Bit_Extender bit_extender_2
  Subtractor #(.width(32)) subtractor_3 (.a(32'h20), .b(B), .out(subtractor_3_out));  // open: bin, bout
  Subtractor #(.width(32)) subtractor_4 (.a(A), .b(B), .out(sub));  // open: bin, bout
  Shifter #(.width(32)) shifter_3 (.in(reverse_1_out_2), .\dist (subtractor_3_out[4:0]), .out(shifter_3_out));
  Shifter #(.width(32), .shift("lr")) shifter_4 (
    .in(shifter_3_out), .\dist (subtractor_3_out[4:0]), .out(shifter_4_out));
  Multiplexer #(.width(32)) multiplexer_1 (
    .in0(32'h20), .in1(bit_extender_1_out), .out(tmp1), .sel(bitfinder_1_found));  // open: en
  Multiplexer #(.width(32)) multiplexer_2 (
    .in0(32'h20), .in1(bit_extender_2_out), .out(tmp2), .sel(bitfinder_2_found));  // open: en
  assign \or  = A | B;  // OR_Gate or_1, 32 bits wide
  assign rev = shifter_2_out | shifter_4_out;  // OR_Gate or_2, 32 bits wide
  Comparator #(.width(32), .mode("unsigned")) comparator_1 (.a(tmp1), .b(tmp2), .eq(out_7));  // open: gt, lt
  Comparator #(.width(32), .mode("unsigned")) comparator_2 (.a(tmp1), .b(tmp2), .gt(out_9));  // open: eq, lt
  Comparator #(.width(32)) comparator_3 (.a(A), .b(B), .eq(zero));  // open: gt, lt
  Multiplexer #(.select(4), .width(32)) multiplexer_3 (
    .in0(add), .in1(sub), .in2(\or ), .in3({B[15:0], {16{1'b0}}}), .in4(sll), .in5(rev), .out(C),
    .sel(ALUopcode));  // open: in6, in7, in8, in9, in10, in11, in12, in13, in14, in15, en

  // Other names for the same wires on the sheet: lui[31:16] = B[15:0]
endmodule

module DM (
  input  [31:0] addr,
  input  [31:0] WD,
  input  clk,
  input  reset,
  input  wr,
  output [31:0] RD
);

  RAM #(.addrWidth(12), .dataWidth(32), .bus("separate")) ram_1 (
    .addr(addr[13:2]), .din(WD), .data(RD), .str(wr), .clk(clk), .clr(reset));  // open: sel, ld
endmodule

module EXT (
  input  [15:0] IMM,
  input  EXTOp,
  output [31:0] extend
);

  wire [31:0] bit_extender_1_out, bit_extender_2_out;

  assign bit_extender_1_out = {{16{1'b0}}, IMM};  // Bit_Extender bit_extender_1
  assign bit_extender_2_out = {{16{IMM[15]}}, IMM};  // Bit_Extender bit_extender_2
  Multiplexer #(.width(32)) multiplexer_1 (
    .in0(bit_extender_1_out), .in1(bit_extender_2_out), .out(extend), .sel(EXTOp));  // open: en
endmodule

module NPC (
  input  [31:0] PC,
  input  zero,
  input  [25:0] IMM,
  input  [2:0] NPCOp,
  input  [31:0] ra,
  input  in_6,
  output [31:0] PC_4,
  output [31:0] NPC
);

  wire [31:0] beq, bit_extender_1_out, multiplexer_1_out, multiplexer_2_out;

  assign bit_extender_1_out = {{14{IMM[15]}}, {IMM[15:0], 2'b00}};  // Bit_Extender bit_extender_1
  Adder #(.width(32)) adder_1 (.a(PC), .b(32'h4), .out(PC_4));  // open: cin, cout
  Adder #(.width(32)) adder_2 (.a(PC_4), .b(bit_extender_1_out), .out(beq));  // open: cin, cout
  Multiplexer #(.width(32)) multiplexer_1 (.in0(PC_4), .in1(beq), .out(multiplexer_1_out), .sel(in_6));  // open: en
  Multiplexer #(.width(32)) multiplexer_2 (.in0(PC_4), .in1(beq), .out(multiplexer_2_out), .sel(zero));  // open: en
  Multiplexer #(.select(3), .width(32)) multiplexer_3 (
    .in0(PC_4), .in1(multiplexer_2_out), .in2({PC[31:28], IMM, 2'b00}), .in3(ra), .in4(multiplexer_1_out),
    .out(NPC), .sel(NPCOp));  // open: in5, in6, in7, en

  // Notes on the sheet:
  //   beq
  //   j
  //   jal
  //   jalr
  //   jr
  //   010
  //   011
endmodule

module CTRL (
  input  in_1,
  input  in_2,
  input  in_3,
  input  [5:0] Funccode,
  input  [5:0] OPcode,
  output [2:0] NPCOp,
  output [2:0] WDSel,
  output BSel,
  output DMWR,
  output extOp,
  output weSel,
  output [2:0] wrA3Sel,
  output [3:0] ALUOp
);

  wire add_out, and_1_out, and_2_out, and_3_out, and_4_out, and_5_out, beq_out, blz_out, j_out, jal_out,
       jalr_out, jr_out, lui_out, lw_out, lwf_out, not_1_out, not_2_out, not_3_out, not_4_out, not_5_out,
       not_6_out, not_7_out, not_8_out, not_9_out, not_10_out, not_11_out, not_12_out, not_13_out,
       not_14_out, not_15_out, not_16_out, ori_out, rev_out, sll_out, special_out, sub_out, sw_out;

  not not_1 (not_1_out, OPcode[5]);
  not not_2 (not_2_out, OPcode[4]);
  not not_3 (not_3_out, OPcode[3]);
  not not_4 (not_4_out, OPcode[2]);
  not not_5 (not_5_out, OPcode[1]);
  not not_6 (not_6_out, OPcode[0]);
  not not_7 (not_7_out, Funccode[5]);
  not not_8 (not_8_out, Funccode[4]);
  not not_9 (not_9_out, Funccode[3]);
  not not_10 (not_10_out, Funccode[2]);
  not not_11 (not_11_out, Funccode[1]);
  not not_12 (not_12_out, Funccode[0]);
  and special (special_out, not_1_out, not_2_out, not_3_out, not_4_out, not_5_out, not_6_out);
  and add (add_out, Funccode[5], not_8_out, not_9_out, special_out, not_10_out, not_11_out, not_12_out);
  and sub (sub_out, Funccode[5], not_8_out, not_9_out, special_out, not_10_out, Funccode[1], not_12_out);
  and ori (ori_out, not_1_out, not_2_out, OPcode[3], OPcode[2], not_5_out, OPcode[0]);
  and lw (lw_out, OPcode[5], not_2_out, not_3_out, not_4_out, OPcode[1], OPcode[0]);
  and sw (sw_out, OPcode[5], not_2_out, OPcode[3], not_4_out, OPcode[1], OPcode[0]);
  and beq (beq_out, not_1_out, not_2_out, not_3_out, OPcode[2], not_5_out, not_6_out);
  and lui (lui_out, not_1_out, not_2_out, OPcode[3], OPcode[2], OPcode[1], OPcode[0]);
  and sll (sll_out, not_1_out, not_2_out, not_3_out, not_4_out, not_5_out, not_6_out, not_7_out, not_8_out, not_9_out, not_10_out, not_11_out, not_12_out);
  and j (j_out, not_1_out, not_2_out, not_3_out, not_4_out, OPcode[1], not_6_out);
  and jal (jal_out, not_1_out, not_2_out, not_3_out, not_4_out, OPcode[1], OPcode[0]);
  and jalr (jalr_out, not_7_out, not_8_out, Funccode[3], special_out, not_10_out, not_11_out, Funccode[0]);
  and jr (jr_out, not_7_out, not_8_out, Funccode[3], special_out, not_10_out, not_11_out, not_12_out);
  and blz (blz_out, not_1_out, OPcode[4], OPcode[3], not_4_out, not_5_out, not_6_out);
  and rev (rev_out, OPcode[5], OPcode[4], not_3_out, not_4_out, not_5_out, not_6_out);
  and lwf (lwf_out, OPcode[5], OPcode[4], OPcode[3], not_4_out, not_5_out, not_6_out);
  buf or_1 (NPCOp[2], blz_out);  // OR_Gate
  or or_2 (NPCOp[1], jr_out, j_out, jal_out, jalr_out);
  and and_1 (and_1_out, lwf_out, in_3);
  buf or_3 (wrA3Sel[2], and_1_out);  // OR_Gate
  or or_4 (NPCOp[0], beq_out, jr_out, jalr_out);
  not not_13 (not_13_out, in_2);
  and and_2 (and_2_out, not_13_out, blz_out);
  or or_5 (wrA3Sel[1], and_2_out, jal_out);
  not not_14 (not_14_out, in_1);
  not not_15 (not_15_out, in_2);
  and and_3 (and_3_out, blz_out, not_15_out, not_14_out);
  or or_6 (wrA3Sel[0], add_out, and_2_out, sub_out, sll_out);
  and and_4 (and_4_out, blz_out, in_1);
  buf or_7 (WDSel[2], and_3_out);  // OR_Gate
  or or_8 (WDSel[1], and_4_out, jalr_out, jal_out);
  or or_9 (WDSel[0], lw_out, and_4_out, lwf_out, 1'b0);
  or or_10 (BSel, rev_out, lw_out, ori_out, sw_out, lui_out, lwf_out);
  buf or_11 (DMWR, sw_out);  // OR_Gate
  or or_12 (extOp, lwf_out, lw_out, sw_out);
  buf or_13 (ALUOp[3], 1'b0);  // OR_Gate
  or or_14 (ALUOp[2], 1'b0, sll_out, rev_out);
  or or_15 (ALUOp[1], ori_out, lui_out);
  and and_5 (and_5_out, not_16_out, blz_out);
  or or_16 (ALUOp[0], rev_out, lui_out, beq_out, sub_out);
  not not_16 (not_16_out, in_2);
  or or_17 (weSel, and_5_out, jalr_out, sll_out, ori_out, lw_out, sub_out, lui_out, add_out, jal_out, rev_out, lwf_out);

  // Other names for the same wires on the sheet: odd_or_even = in_3; tunnel = in_2; tunnel_t = in_1

  // Notes on the sheet:
  //   001101
  //   100011
  //   101011
  //   000100
  //   001111
  //   000010
  //   000011
  //   001001
  //   001000
  //   011000
  //   110000
  //   111000
  //   想写入就得enable
endmodule

module reverse (
  input  [31:0] in_1,
  output [31:0] out_2
);


  assign out_2 = {in_1[0], in_1[1], in_1[2], in_1[3], in_1[4], in_1[5], in_1[6], in_1[7], in_1[8], in_1[9], in_1[10], in_1[11], in_1[12], in_1[13], in_1[14], in_1[15], in_1[16], in_1[17], in_1[18], in_1[19], in_1[20], in_1[21], in_1[22], in_1[23], in_1[24], in_1[25], in_1[26], in_1[27], in_1[28], in_1[29], in_1[30], in_1[31]};
endmodule

module LWF (
  input  [31:0] offset,
  input  [31:0] rt,
  output out_3
);

  wire [5:1] bitadder_1_out;
  wire [31:0] and_1_out;

  assign and_1_out = offset & rt;  // AND_Gate and_1, 32 bits wide
  BitAdder #(.width(32)) bitadder_1 (.in0(and_1_out), .out({bitadder_1_out, out_3}));

  // Notes on the sheet:
  //   1奇0偶
endmodule
